# Fritzing sketch Steckplatine-LEDs (saved by Fritzing 0.9.2b)
breadboards: 1

parts:
  SHIFT1 = TPIC6B595
  Raspberry_Pi2 = Raspberry Pi 2
  LED12 = LED - 5mm [color="Red (633nm)" package="5 mm [THT]"]
  LED13 = LED - 5mm [color="Red (633nm)" package="5 mm [THT]"]
  LED14 = LED - 5mm [color="Red (633nm)" package="5 mm [THT]"]
  LED15 = LED - 5mm [color="Red (633nm)" package="5 mm [THT]"]
  LED16 = LED - 5mm [color="Red (633nm)" package="5 mm [THT]"]
  R15 = Resistor [tolerance=±5% resistance=150 package=THT]
  R16 = Resistor [tolerance=±5% resistance=150 package=THT]
  R17 = Resistor [tolerance=±5% resistance=150 package=THT]
  R18 = Resistor [tolerance=±5% resistance=150 package=THT]
  R19 = Resistor [tolerance=±5% resistance=150 package=THT]

nets:
  N1: SHIFT1.SER_IN, Raspberry_Pi2.GPIO8, Raspberry_Pi2.GPIO25
  N2: SHIFT1.DRAIN0, LED12.cathode
  N3: SHIFT1.DRAIN1, LED14.cathode
  N4: SHIFT1.DRAIN2, LED13.cathode
  N5: SHIFT1.DRAIN3, LED15.cathode
  VCC: SHIFT1.SRCLR, SHIFT1.VCC, Raspberry_Pi2.5V, R15.Pin_1, R16.Pin_1, R17.Pin_1, R18.Pin_1, R19.Pin_1
  GND: SHIFT1.G, SHIFT1.GND, SHIFT1.RCK, Raspberry_Pi2.GND, Raspberry_Pi2.GPIO24
  N6: SHIFT1.SRCK, Raspberry_Pi2.GPIO23
  N7: SHIFT1.DRAIN4, LED16.cathode
  N8: LED12.anode, R19.Pin_0
  N9: LED13.anode, R16.Pin_0
  N10: LED14.anode, R18.Pin_0
  N11: LED15.anode, R15.Pin_0
  N12: LED16.anode, R17.Pin_0

custom parts:
  TPIC6B595: 8-bit high-power parallel-load shift register
