# Fritzing sketch Steckplatine-Taster (saved by Fritzing 0.9.2b)
breadboards: 1

parts:
  Raspberry_Pi2 = Raspberry Pi 2
  S2 = Pushbutton [package="[THT]"]
  S3 = Pushbutton [package="[THT]"]
  S4 = Pushbutton [package="[THT]"]
  S5 = Pushbutton [package="[THT]"]
  S6 = Pushbutton [package="[THT]"]
  S7 = Pushbutton [package="[THT]"]
  S8 = Pushbutton [package="[THT]"]

nets:
  N1: Raspberry_Pi2.GPIO5, Raspberry_Pi2.GND, Raspberry_Pi2.GPIO14, S2.Pin_1, S2.Pin_2, S3.Pin_1, S3.Pin_2, S4.Pin_1, S4.Pin_2, S5.Pin_1, S5.Pin_2, S6.Pin_1, S6.Pin_2, S7.Pin_1, S7.Pin_2, S8.Pin_1, S8.Pin_2, S8.Pin_3, S8.Pin_4
  N2: Raspberry_Pi2.GPIO6, S7.Pin_3, S7.Pin_4
  N3: Raspberry_Pi2.GPIO19, S2.Pin_3, S2.Pin_4
  N4: Raspberry_Pi2.GPIO26, Raspberry_Pi2.GPIO21, S3.Pin_3, S3.Pin_4
  N5: Raspberry_Pi2.GPIO20, S4.Pin_3, S4.Pin_4
  N6: Raspberry_Pi2.GPIO16, S5.Pin_3, S5.Pin_4
  N7: Raspberry_Pi2.GPIO12, Raspberry_Pi2.GPIO25, S6.Pin_3, S6.Pin_4
